// Logisim project Circuit.circ as structural Verilog: 11 circuits, main circuit main
// 0
module main (
);

  wire B0, B1, B2, B3, B4, B5, B6, B7, B8, B9, BDiv, BMult, BSub, BSum, C, NumberEn, OpEn, pulse_1_output,
       pulse_2_output, tunnel;
  wire [1:0] operation;
  wire [3:0] display, Number, processor_1_probea, processor_1_probeb;
  wire [24:0] Op_display;

  Button _1 (.out(B1));
  Button _4 (.out(B4));
  Button _7 (.out(B7));
  Button u_C (.out(C));
  Button _2 (.out(B2));
  Button _5 (.out(B5));
  Button _8 (.out(B8));
  Button _0 (.out(B0));
  operation_control operation_control (
    .sum(BSum), .sub(BSub), .mult(BMult), .div(BDiv), .Enable(OpEn), .Operation(operation),
    .Data(Op_display), .Reset(C));
  number_control number_control (
    ._0(B0), ._1(B1), ._2(B2), ._3(B3), ._4(B4), ._5(B5), ._6(B6), ._7(B7), ._8(B8), ._9(B9), .Data(Number),
    .Enable(NumberEn));
  Button button (.out(BSum));
  Button _3 (.out(B3));
  Button button_2 (.out(BSub));
  Button _6 (.out(B6));
  Button x (.out(BMult));
  Button _9 (.out(B9));
  Button button_3 (.out(BDiv));
  Button button_4 (.out(tunnel));
  DotMatrix #(.matrixrows(5)) dotmatrix_1 (
    .col0(Op_display[24:20]), .col1(Op_display[19:15]), .col2(Op_display[14:10]), .col3(Op_display[9:5]),
    .col4(Op_display[4:0]));
  pulse pulse_1 (.Button(OpEn), .Output(pulse_1_output));
  pulse pulse_2 (.Button(tunnel), .Output(pulse_2_output));
  Hex_Digit_Display hex_digit_display_1 (.value(display));  // open: dp
  processor processor_1 (
    .num_data(Number), .num_en(NumberEn), .op_data(operation), .op_en(pulse_1_output), .reset(C),
    .probeA(processor_1_probea), .probeB(processor_1_probeb), .Result(display), .equal(pulse_2_output));
  // Probe on processor_1_probea
  // Probe on processor_1_probeb
  // Probe on display
  // Probe on display
endmodule

module latchSR (
  input  Set,
  input  Reset,
  output out_3
);

  wire and_1_out, and_2_out, not_2_out;

  and and_1 (and_1_out, Set, not_2_out);
  and and_2 (and_2_out, out_3, Reset);
  not not_1 (out_3, and_1_out);
  not not_2 (not_2_out, and_2_out);
endmodule

module latchD (
  input  D,
  input  Enable,
  output out_3
);

  wire and_1_out, and_2_out, not_1_out, not_2_out, not_3_out;

  not not_1 (not_1_out, D);
  and and_1 (and_1_out, D, Enable);
  not not_2 (not_2_out, and_1_out);
  not not_3 (not_3_out, and_2_out);
  and and_2 (and_2_out, Enable, not_1_out);
  latchSR latchsr_1 (.Set(not_2_out), .Reset(not_3_out), .out_3(out_3));
endmodule

module flip_flop (
  input  D,
  input  Enable,
  input  Clock,
  output out_4
);

  wire and_1_out, latchd_1_out_3, not_1_out;

  and and_1 (and_1_out, Enable, Clock);
  not not_1 (not_1_out, Clock);
  latchD latchd_1 (.D(D), .Enable(and_1_out), .out_3(latchd_1_out_3));
  latchD latchd_2 (.D(latchd_1_out_3), .Enable(not_1_out), .out_3(out_4));
endmodule

module pulse (
  input  Button,
  output Output
);

  wire Clock_out, flip_flop_1_out_4, flip_flop_2_out_4, not_1_out;

  Clock Clock (.out(Clock_out));
  flip_flop flip_flop_1 (.D(Button), .Enable(1'b1), .Clock(Clock_out), .out_4(flip_flop_1_out_4));
  not not_1 (not_1_out, flip_flop_2_out_4);
  flip_flop flip_flop_2 (.D(flip_flop_1_out_4), .Enable(1'b1), .Clock(Clock_out), .out_4(flip_flop_2_out_4));
  and and_1 (Output, Button, not_1_out);

  // Notes on the sheet:
  //   Enable
endmodule

module registradores (
  input  Clock,
  input  Enable,
  input  Reset,
  input  [1:0] AddresA,
  input  [1:0] AddresB,
  input  [3:0] Data,
  output [3:0] DataA,
  output [3:0] DataB
);

  wire en0, en1, en2;
  wire [3:0] out0, out1, out2;

  Demultiplexer #(.select(2)) demultiplexer_1 (
    .out0(en0), .out1(en1), .out2(en2), .in(Enable), .sel(AddresA));  // open: out3, en
  Register #(.width(4)) register_1 (.D(Data), .en(en0), .Q(out0), .clk(Clock), .clr(Reset));
  Register #(.width(4)) register_2 (.D(Data), .en(en1), .Q(out1), .clk(Clock), .clr(Reset));
  Multiplexer #(.select(2), .width(4)) multiplexer_1 (
    .in0(out0), .in1(out1), .in2(out2), .out(DataA), .sel(AddresA));  // open: in3, en
  Multiplexer #(.select(2), .width(4)) multiplexer_2 (
    .in0(out0), .in1(out1), .in2(out2), .out(DataB), .sel(AddresB));  // open: in3, en
  Register #(.width(4)) register_3 (.D(Data), .en(en2), .Q(out2), .clk(Clock), .clr(Reset));

  // Other names for the same wires on the sheet: addA[1:0] = AddresA; addB[1:0] = AddresB; clk = Clock; en = Enable;
  //   rst = Reset
endmodule

module ULA (
  input  [3:0] IA,
  input  [3:0] IB,
  input  [1:0] Control,
  output [3:0] out_4
);

  wire [3:0] Div, Mult, Sub, Sum;

  Adder #(.width(4)) adder_1 (.a(IB), .b(IA), .out(Sum));  // open: cin, cout
  Subtractor #(.width(4)) subtractor_1 (.a(IB), .b(IA), .out(Sub));  // open: bin, bout
  Multiplier #(.width(4)) multiplier_1 (.a(IB), .b(IA), .out(Mult));  // open: cin, cout
  Divider #(.width(4)) divider_1 (.a(IB), .b(IA), .out(Div));  // open: upper, rem
  Multiplexer #(.select(2), .width(4)) multiplexer_1 (
    .in0(Sum), .in1(Sub), .in2(Mult), .in3(Div), .out(out_4), .sel(Control));  // open: en

  // Other names for the same wires on the sheet: IA_t[3:0] = IB; IB_t[3:0] = IA
endmodule

module number_control (
  input  _0,
  input  _1,
  input  _2,
  input  _3,
  input  _4,
  input  _5,
  input  _6,
  input  _7,
  input  _8,
  input  _9,
  output [3:0] Data,
  output Enable
);

  wire [3:0] Out0, Out1, Out2, Out3, Out4, Out5, Out6, Out7, Out8, Out9;

  Multiplexer #(.width(4)) multiplexer_1 (.in0(4'b0000), .in1(4'b0000), .out(Out0), .sel(_0));  // open: en
  Multiplexer #(.width(4)) multiplexer_2 (.in0(4'b0000), .in1(4'b0100), .out(Out4), .sel(_4));  // open: en
  Multiplexer #(.width(4)) multiplexer_3 (.in0(4'b0000), .in1(4'b1000), .out(Out8), .sel(_8));  // open: en
  Multiplexer #(.width(4)) multiplexer_4 (.in0(4'b0000), .in1(4'b0001), .out(Out1), .sel(_1));  // open: en
  Multiplexer #(.width(4)) multiplexer_5 (.in0(4'b0000), .in1(4'b0101), .out(Out5), .sel(_5));  // open: en
  Multiplexer #(.width(4)) multiplexer_6 (.in0(4'b0000), .in1(4'b1001), .out(Out9), .sel(_9));  // open: en
  Multiplexer #(.width(4)) multiplexer_7 (.in0(4'b0000), .in1(4'b0010), .out(Out2), .sel(_2));  // open: en
  Multiplexer #(.width(4)) multiplexer_8 (.in0(4'b0000), .in1(4'b0110), .out(Out6), .sel(_6));  // open: en
  assign Data = Out0 | Out1 | Out2 | Out3 | Out4 | Out5 | Out6 | Out7 | Out8 | Out9;  // OR_Gate or_1, 4 bits wide
  or or_2 (Enable, _0, _1, _2, _3, _4, _5, _6, _7, _8, _9);
  Multiplexer #(.width(4)) multiplexer_9 (.in0(4'b0000), .in1(4'b0011), .out(Out3), .sel(_3));  // open: en
  Multiplexer #(.width(4)) multiplexer_10 (.in0(4'b0000), .in1(4'b0111), .out(Out7), .sel(_7));  // open: en

  // Other names for the same wires on the sheet: I0 = _0; I1 = _1; I2 = _2; I3 = _3; I4 = _4; I5 = _5; I6 = _6;
  //   I7 = _7; I8 = _8; I9 = _9
endmodule

module operation_control (
  input  sum,
  input  sub,
  input  mult,
  input  div,
  input  Reset,
  output Enable,
  output [1:0] Operation,
  output [24:0] Data
);

  wire clock_1_out, clock_2_out;
  wire [1:0] multiplexer_5_out, multiplexer_6_out, multiplexer_7_out, multiplexer_8_out, SelectedOperation;
  wire [24:0] divOut, multOut, OperationSignal, subOut, sumOut;

  Multiplexer #(.width(25)) multiplexer_1 (.in0({25{1'b0}}), .in1(25'h23880), .out(sumOut), .sel(sum));  // open: en
  Multiplexer #(.width(25)) multiplexer_2 (.in0({25{1'b0}}), .in1(25'h21080), .out(subOut), .sel(sub));  // open: en
  Multiplexer #(.width(25)) multiplexer_3 (.in0({25{1'b0}}), .in1(25'h51140), .out(multOut), .sel(mult));  // open: en
  Multiplexer #(.width(25)) multiplexer_4 (.in0({25{1'b0}}), .in1(25'h25480), .out(divOut), .sel(div));  // open: en
  assign OperationSignal = sumOut | subOut | multOut | divOut;  // OR_Gate or_1, 25 bits wide
  or or_2 (Enable, sum, sub, mult, div);
  Register #(.width(2)) register_1 (.D(SelectedOperation), .en(Enable), .Q(Operation), .clk(clock_1_out), .clr(Reset));
  Clock clock_1 (.out(clock_1_out));
  Register #(.width(25)) register_2 (.D(OperationSignal), .en(Enable), .Q(Data), .clk(clock_2_out), .clr(Reset));
  Clock clock_2 (.out(clock_2_out));
  Multiplexer #(.width(2)) multiplexer_5 (.in0(2'b00), .in1(2'b00), .out(multiplexer_5_out), .sel(sum));  // open: en
  Multiplexer #(.width(2)) multiplexer_6 (.in0(2'b00), .in1(2'b01), .out(multiplexer_6_out), .sel(sub));  // open: en
  Multiplexer #(.width(2)) multiplexer_7 (.in0(2'b00), .in1(2'b10), .out(multiplexer_7_out), .sel(mult));  // open: en
  Multiplexer #(.width(2)) multiplexer_8 (.in0(2'b00), .in1(2'b11), .out(multiplexer_8_out), .sel(div));  // open: en
  ExactlyOne xor_1[1:0] (
    .out(SelectedOperation), .in0(multiplexer_5_out), .in1(multiplexer_6_out), .in2(multiplexer_7_out),
    .in3(multiplexer_8_out));

  // Other names for the same wires on the sheet: en = Enable
endmodule

module processor (
  input  [3:0] num_data,
  input  num_en,
  input  [1:0] op_data,
  input  op_en,
  input  reset,
  input  equal,
  output [3:0] probeA,
  output [3:0] probeB,
  output [3:0] Result
);

  wire act_en, clock_1_out, en;
  wire [1:0] multiplexer_1_out, multiplexer_3_out, multiplexer_4_out;
  wire [3:0] multiplexer_2_out, ula_1_out_4;

  or or_1 (act_en, op_en, equal);
  Multiplexer #(.width(2)) multiplexer_1 (.in0(2'b00), .in1(2'b01), .out(multiplexer_1_out), .sel(op_en));  // open: en
  Multiplexer #(.width(4)) multiplexer_2 (
    .in0(ula_1_out_4), .in1(num_data), .out(multiplexer_2_out), .sel(num_en));  // open: en
  Multiplexer #(.width(2)) multiplexer_3 (.in0(2'b01), .in1(2'b00), .out(multiplexer_3_out), .sel(op_en));  // open: en
  Clock clock_1 (.out(clock_1_out));
  registradores registradores_1 (
    .Clock(clock_1_out), .Enable(en), .Reset(reset), .AddresA(multiplexer_1_out),
    .AddresB(multiplexer_3_out), .Data(multiplexer_2_out), .DataA(probeA), .DataB(probeB));
  ULA ula_1 (.IA(probeA), .IB(probeB), .Control(multiplexer_4_out), .out_4(ula_1_out_4));
  Multiplexer #(.width(2)) multiplexer_4 (
    .in0(op_data), .in1(2'b00), .out(multiplexer_4_out), .sel(op_en));  // open: en
  or or_2 (en, num_en, equal, op_en);
  // Probe on ula_1_out_4

  assign Result = probeA;

  // Other names for the same wires on the sheet: data[3:0] = num_data; op[1:0] = op_data
endmodule

module drafts (
  output Output
);

  wire clock_1_out, d_ff_1_q, d_ff_2_q, not_1_out, not_2_out, undriven;

  Clock clock_1 (.out(clock_1_out));
  not not_1 (not_1_out, clock_1_out);
  D_Flip_Flop d_ff_1 (.clk(clock_1_out), .D(undriven), .Q(d_ff_1_q));  // open: Qn, preset, en, reset
  D_Flip_Flop d_ff_2 (.clk(not_1_out), .D(d_ff_1_q), .Q(d_ff_2_q));  // open: Qn, preset, en, reset
  not not_2 (not_2_out, d_ff_2_q);
  and and_1 (Output, not_2_out, undriven);
endmodule
